# Fritzing sketch Control Surface Prototype (saved by Fritzing 0.9.5d)
breadboards: 2

parts:
  S1 = Pushbutton [package="[THT]"]
  S2 = Momentary Switch [package=ksa_sealed_tac_switch]
  S3 = Momentary Switch [package=ksa_sealed_tac_switch]
  S4 = Momentary Switch [package=ksa_sealed_tac_switch]
  R1 = Rotary Potentiometer (Small) [maximum_resistance=100kΩ package=THT]
  R2 = Rotary Potentiometer (Small) [maximum_resistance=100kΩ package=THT]
  R3 = Slide Potentiometer [maximum_resistance=100kΩ]  # not connected
  Grove1 = Grove OLED 128x96
  CPU1 = NodeMCU WROOM ESP 32
  S5 = Pushbutton [package="[THT]"]
  S6 = Momentary Switch [package=ksa_sealed_tac_switch]
  S7 = Momentary Switch [package=ksa_sealed_tac_switch]
  S8 = Momentary Switch [package=ksa_sealed_tac_switch]
  U1 = ENCODER-QUADRATURE [package=encoder-16mm-quad]
  Grove2 = Grove OLED 128x96  # not connected
  R4 = Slide Potentiometer [maximum_resistance=100kΩ]  # not connected
  S11 = Pushbutton [package="[THT]"]
  S12 = Pushbutton [package="[THT]"]
  S13 = Pushbutton [package="[THT]"]
  S14 = Pushbutton [package="[THT]"]
  R5 = Rotary Potentiometer (Small) [maximum_resistance=100kΩ package=THT]
  R6 = Rotary Potentiometer (Small) [maximum_resistance=100kΩ package=THT]
  R7 = Slide Potentiometer [maximum_resistance=100kΩ]  # not connected
  Part2 = Arduino Nano (Rev3.0) (ICSP)  # not connected
  Part3 = Thumb Joystick

nets:
  N1: S1.Pin_1, S1.Pin_2
  GND: S1.Pin_3, S1.Pin_4, S2.4, S3.4, S4.4, R1.leg1, R2.leg1, Grove1.GND, S6.3, S6.4, S7.4, S8.4, U1.B, Part3.GND
  VCC: R1.leg2, R2.leg2, Grove1.VCC, Part3.VCC
  N2: Grove1.SDA, CPU1.pin_30
  N3: Grove1.SCL, CPU1.pin_27
  N4: CPU1.pin_24, CPU1.pin_28
  N5: S5.Pin_1, S5.Pin_2
  N6: S5.Pin_3, S5.Pin_4
  N7: S6.1, S6.2
  N8: S11.Pin_1, S11.Pin_2
  N9: S11.Pin_3, S11.Pin_4, S12.Pin_3, S12.Pin_4, S13.Pin_3, S13.Pin_4, S14.Pin_3, S14.Pin_4, R5.leg1, R6.leg1
  N10: S12.Pin_1, S12.Pin_2
  N11: S13.Pin_1, S13.Pin_2
  N12: S14.Pin_1, S14.Pin_2
  N13: R5.leg2, R6.leg2

custom parts:
  NodeMCU WROOM ESP 32: 30 pol Development Kit
